// Logisim project project3.circ as structural Verilog: 1 circuit, main circuit main
module main (
  input  in_1,
  input  [3:0] in_2,
  input  in_3,
  input  [1:0] in_4,
  input  [3:0] in_5,
  input  [1:0] in_6,
  input  [3:0] in_7,
  input  [1:0] in_8,
  input  [1:0] in_9,
  input  in_10,
  input  in_11,
  input  [1:0] in_12,
  input  in_13,
  input  [1:0] in_14,
  output [7:0] out_15,
  output [3:0] out_16
);

  wire clock_1_out;

  Clock clock_1 (.out(clock_1_out));
  part2_main main_1 (
    .OutASel(in_8), .OutBSel(in_8), .FunSel_2(in_4), .RegSel(in_5), .MuxASel(in_9), .OutCSel(in_8),
    .OutDSel(in_8), .FunSel_3(in_6), .RegSel_2(in_7), .L_H(in_11), .Enable(in_13), .FunSel_4(in_14),
    .MuxCSel(in_10), .MuxBSel(in_12), .FunSel(in_2), .out_21(out_15), .in_10(in_3), .in_11(in_3),
    .in_12(in_3), .in_13(in_1), .in_2(clock_1_out), .out_22(out_16));
endmodule
